# Fritzing sketch Arduino_Sense (saved by Fritzing 0.9.3b)
breadboards: 1

parts:
  Part1 = Arduino Nano 33 BLE Sense
  Grove1 = Grove OLED 128x96

nets:
  GND: Part1.GND, Part1.A7, Grove1.GND
  N1: Part1.D11/MOSI, Part1.+5V
  N2: Part1.A5, Grove1.SCL
  N3: Part1.A4, Grove1.SDA
  3V3: Part1.3V3, Grove1.VCC

custom parts:
  Arduino Nano 33 BLE Sense: The Nano 33 BLE Sense (without headers) is Arduino’s 3.3V AI enabled board in the smallest available form factor: 45x18mm! The Arduino Nano 33 BLE Sense is a completely new board on a well-known form factor. It comes with a series of embedded sensors: 9 axis inertial sensor: what makes this board ideal for wearable devices humidity, and temperature sensor: to get highly accurate measurements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
